# Fritzing sketch clockFritz (saved by Fritzing 0.9.9b)
breadboards: 3

parts:
  Breadboard4 = Breadboard Split Power
  Breadboard5 = Breadboard Split Power
  Teensy_3_1 = Teensy 3.1
  WIZ820io1 = WIZ820io [part_number=WIZ820io]
  Grove1 = Grove 4 Digit Display
  RG_encoder1 = SprkFn RG Encoder [package="DIP (Dual Inline) [THT]"]
  C1 = Tantalum Capacitor [capacitance="1 μF" voltage=35V package="B 3528 [SMD, tantalum]"]
  C2 = Tantalum Capacitor [capacitance="1 μF" voltage=35V package="B 3528 [SMD, tantalum]"]
  J1 = Piezo Speaker
  OLED_I2C1 = OLED 128x64 I2C Monochrome Display
  S1 = Pushbutton [package="[THT]"]
  S2 = Pushbutton [package="[THT]"]
  PIR1 = PIR sensor

nets:
  GND: Breadboard4.pin3Z, Breadboard4.pin20Z, Breadboard4.pin29Z, Breadboard5.pin3Z, Breadboard5.pin11Z, Breadboard5.pin28Z, Teensy_3_1.GND, WIZ820io1.GND, Grove1.GND, RG_encoder1.GND, RG_encoder1.B, C1.-, C2.-, J1.pin1, OLED_I2C1.GND, S1.Pin_3, S1.Pin_4, S2.Pin_3, S2.Pin_4, PIR1.GND
  VDD: Breadboard4.pin4Y, Breadboard4.pin15Y, Breadboard4.pin17Y, Breadboard4.pin21Y, Breadboard4.pin29Y, Breadboard5.pin3Y, Breadboard5.pin12Y, Breadboard5.pin15Y, Breadboard5.pin17Y, Breadboard5.pin29Y, Teensy_3_1.3V3, WIZ820io1.VIN, Grove1.VCC, OLED_I2C1.VDD, PIR1.VDD
  N1: Teensy_3_1.D1, PIR1.SIG
  N2: Teensy_3_1.D2, S1.Pin_1, S1.Pin_2
  N3: Teensy_3_1.D3, S2.Pin_1, S2.Pin_2
  N4: Teensy_3_1.D5, RG_encoder1.A, C2.+
  N5: Teensy_3_1.D6, RG_encoder1.C, C1.+
  N6: Teensy_3_1.D9, WIZ820io1.nRESET
  N7: Teensy_3_1.D10, WIZ820io1.nSS
  N8: Teensy_3_1.D11, WIZ820io1.MOSI
  N9: Teensy_3_1.D12, WIZ820io1.MISO
  N10: Teensy_3_1.D13, WIZ820io1.SCLK
  N11: Teensy_3_1.A0/D14, RG_encoder1.SW
  N12: Teensy_3_1.A4/D18, OLED_I2C1.SDA
  N13: Teensy_3_1.A5/D19, OLED_I2C1.SCK
  N14: Teensy_3_1.A6/D20, Grove1.DIO
  N15: Teensy_3_1.A7/D21, Grove1.CLK
  N16: Teensy_3_1.A9/D23, J1.pin2

custom parts:
  Breadboard Split Power: A custom 6 pin per group power supply strip where the top row (ground) is all bussed together and the bottom row (+V) is split in two groups of 12 pins. This version is modified to be a loadable part and was rescaled to be on the standard 1px = 1thou grid with the size set in inches
  SprkFn RG Encoder: SparkFun RG Rotary Encoder
  Pushbutton: A generic pushbutton.
  Pushbutton: A generic pushbutton.
